// Logisim project new_datapath.circ as structural Verilog: 1 circuit, main circuit main
module main (
  input  [1:0] P1_MOVE,
  input  [1:0] P2_MOVE,
  input  START,
  output [4:0] TOTAL,
  output [1:0] WINNING_PLAYER,
  output ENDABLE,
  output W1,
  output W2
);

  wire adder_2_cout, and_1_out, and_2_out, and_3_out, and_4_out, CLK_out, comparator_1_eq, comparator_2_eq,
       comparator_3_eq, comparator_4_eq, comparator_5_eq, comparator_6_eq, comparator_7_eq, comparator_8_eq,
       comparator_9_eq, comparator_10_eq, comparator_11_eq, comparator_12_eq, comparator_13_eq,
       comparator_16_eq, multiplexer_4_out, multiplexer_5_out, multiplexer_6_out, nor_1_out, not_1_out,
       or_1_out, or_2_out, or_3_out, WIN1_out, WIN2_out, xor_1_out;
  wire [1:0] adder_4_out, ADV_q, multiplexer_1_out, multiplexer_2_out, multiplexer_11_out,
       multiplexer_14_out, multiplexer_15_out, subtractor_1_out;
  wire [4:0] adder_1_out, adder_2_out, adder_3_out, multiplexer_8_out, multiplexer_9_out, multiplexer_10_out,
       multiplexer_12_out, multiplexer_13_out, register_1_q;

  Comparator #(.mode("unsigned"), .width(2)) comparator_1 (
    .a(P1_MOVE), .b(2'b01), .eq(comparator_1_eq));  // open: gt, lt
  Comparator #(.mode("unsigned"), .width(2)) comparator_2 (
    .a(P2_MOVE), .b(2'b11), .eq(comparator_2_eq));  // open: gt, lt
  and and_1 (and_1_out, comparator_1_eq, comparator_2_eq);
  Comparator #(.mode("unsigned"), .width(2)) comparator_3 (
    .a(WINNING_PLAYER), .b(2'b01), .eq(comparator_3_eq));  // open: gt, lt
  Comparator #(.mode("unsigned"), .width(2)) comparator_4 (
    .a(WINNING_PLAYER), .b(2'b11), .eq(comparator_4_eq));  // open: gt, lt
  Comparator #(.mode("unsigned"), .width(2)) comparator_5 (
    .a(WINNING_PLAYER), .b(2'b00), .eq(comparator_5_eq));  // open: gt, lt
  Comparator #(.mode("unsigned"), .width(2)) comparator_6 (
    .a(WINNING_PLAYER), .b(2'b10), .eq(comparator_6_eq));  // open: gt, lt
  nor nor_1 (nor_1_out, comparator_4_eq, comparator_5_eq);
  Comparator #(.mode("unsigned"), .width(2)) comparator_7 (
    .a(P1_MOVE), .b(2'b10), .eq(comparator_7_eq));  // open: gt, lt
  Comparator #(.mode("unsigned"), .width(2)) comparator_8 (
    .a(P2_MOVE), .b(2'b01), .eq(comparator_8_eq));  // open: gt, lt
  and and_2 (and_2_out, comparator_7_eq, comparator_8_eq);
  or or_1 (or_1_out, and_1_out, and_2_out, and_3_out);
  Multiplexer #(.width(2)) multiplexer_1 (.in0(2'b10), .in1(2'b01), .out(multiplexer_1_out), .sel(or_1_out));
  Multiplexer #(.width(2)) multiplexer_2 (
    .in0(multiplexer_1_out), .in1(2'b00), .out(multiplexer_2_out), .sel(or_2_out));
  and WIN1 (WIN1_out, comparator_3_eq, nor_1_out);
  and WIN2 (WIN2_out, nor_1_out, comparator_6_eq);
  Comparator #(.mode("unsigned"), .width(2)) comparator_9 (
    .a(P1_MOVE), .b(2'b11), .eq(comparator_9_eq));  // open: gt, lt
  Multiplexer #(.width(2)) multiplexer_3 (.in0(multiplexer_2_out), .in1(2'b11), .out(WINNING_PLAYER), .sel(and_4_out));
  Multiplexer multiplexer_4 (.in0(WIN1_out), .in1(1'b0), .out(multiplexer_4_out), .sel(START));
  Multiplexer multiplexer_5 (.in0(comparator_4_eq), .in1(1'b0), .out(multiplexer_5_out), .sel(START));
  Multiplexer multiplexer_6 (.in0(comparator_5_eq), .in1(1'b0), .out(multiplexer_6_out), .sel(START));
  Multiplexer multiplexer_7 (.in0(WIN2_out), .in1(1'b0), .sel(START));  // open: out
  Comparator #(.mode("unsigned"), .width(2)) comparator_10 (
    .a(P2_MOVE), .b(2'b10), .eq(comparator_10_eq));  // open: gt, lt
  and and_3 (and_3_out, comparator_9_eq, comparator_10_eq);
  Comparator #(.mode("unsigned"), .width(2)) comparator_11 (
    .a(P1_MOVE), .b(2'b00), .eq(comparator_11_eq));  // open: gt, lt
  Comparator #(.mode("unsigned"), .width(2)) comparator_12 (
    .a(P2_MOVE), .b(2'b00), .eq(comparator_12_eq));  // open: gt, lt
  or or_2 (or_2_out, comparator_11_eq, comparator_12_eq);
  not not_1 (not_1_out, or_2_out);
  and and_4 (and_4_out, not_1_out, comparator_13_eq);
  Clock CLK (.out(CLK_out));
  Comparator #(.mode("unsigned"), .width(2)) comparator_13 (
    .a(P2_MOVE), .b(P1_MOVE), .eq(comparator_13_eq));  // open: gt, lt
  Adder #(.width(5)) adder_1 (.a(register_1_q), .b(5'b00001), .out(adder_1_out));  // open: cin, cout
  Multiplexer #(.width(5)) multiplexer_8 (
    .in0(adder_1_out), .in1(register_1_q), .out(multiplexer_8_out), .sel(multiplexer_6_out));
  Multiplexer #(.width(5)) multiplexer_9 (
    .in0(multiplexer_8_out), .in1({5{1'b0}}), .out(multiplexer_9_out), .sel(START));
  Multiplexer #(.select(2), .width(5)) multiplexer_10 (
    .in0({5{1'b0}}), .in1(5'b00100), .in2(5'b01000), .in3(5'b01100), .out(multiplexer_10_out), .sel(P1_MOVE));
  Multiplexer #(.width(2)) multiplexer_11 (
    .in0(multiplexer_15_out), .in1(2'b10), .out(multiplexer_11_out), .sel(START));
  Register #(.width(5)) register_1 (.D(multiplexer_9_out), .Q(register_1_q), .clk(CLK_out));  // open: en, clr
  Multiplexer #(.select(2), .width(5)) multiplexer_12 (
    .in0({5{1'b0}}), .in1(5'b00001), .in2(5'b00010), .in3(5'b00011), .out(multiplexer_12_out), .sel(P2_MOVE));
  Adder #(.width(5)) adder_2 (
    .a(multiplexer_12_out), .b(multiplexer_10_out), .out(adder_2_out), .cout(adder_2_cout));  // open: cin
  Register #(.width(2)) ADV (.D(multiplexer_11_out), .Q(ADV_q), .clk(CLK_out));  // open: en, clr
  or or_3 (or_3_out, multiplexer_5_out, multiplexer_6_out);
  Comparator #(.mode("unsigned"), .width(2)) comparator_14 (
    .a(multiplexer_15_out), .b(2'b10), .eq(W1));  // open: gt, lt
  Comparator #(.mode("unsigned"), .width(2)) comparator_15 (
    .a(multiplexer_15_out), .b(2'b10), .eq(W2));  // open: gt, lt
  Comparator #(.mode("unsigned"), .width(5)) comparator_16 (
    .a(register_1_q), .b(TOTAL), .eq(comparator_16_eq));  // open: gt, lt
  Adder #(.width(5)) adder_3 (.a(adder_2_out), .b(5'b00100), .out(adder_3_out));  // open: cin, cout
  Multiplexer #(.width(5)) multiplexer_13 (.in0(TOTAL), .in1(adder_3_out), .out(multiplexer_13_out), .sel(START));
  Register #(.width(5)) FINAL (.D(multiplexer_13_out), .Q(TOTAL), .clk(CLK_out));  // open: en, clr
  Adder #(.width(2)) adder_4 (.a(ADV_q), .b(2'b01), .out(adder_4_out));  // open: cin, cout
  xor xor_1 (xor_1_out, W1, W2);
  Subtractor #(.width(2)) subtractor_1 (.a(ADV_q), .b(2'b01), .out(subtractor_1_out));  // open: bin, bout
  Multiplexer #(.width(2)) multiplexer_14 (
    .in0(adder_4_out), .in1(subtractor_1_out), .out(multiplexer_14_out), .sel(multiplexer_4_out));
  Multiplexer #(.width(2)) multiplexer_15 (
    .in0(multiplexer_14_out), .in1(ADV_q), .out(multiplexer_15_out), .sel(or_3_out));
  or or_4 (ENDABLE, xor_1_out, comparator_16_eq);

  // Notes on the sheet:
  //   MANCHE WINNER LOGIC
  //   I: winning player
  //   CONTROL SIGNALS
  //   O: winning player
  //   SELECT: invalid
  //   SELECT: start signal
  //   I: final manche
  //   END GAME
  //   I: invalid
  //   I: draw
  //   SET TOTAL MANCHE
  //   ADVANTAGE CALCULATOR
  //   SELECT: start signal
  //   I: clock
  //   I: advantage ( - : player 1, + : player 2)
  //   O: advantage ( - : player 1, + : player 2)
  //   NOTE:
  //   1 manca il controllo sulla mossa precedente
  //   3 la logica total manche sara' riassunta con una logica combinatoria personalizzata
  //   2 la logica winning manche sara' riassunta con una logica combinatoria personalizzata
endmodule
